# Fritzing sketch doorbell (saved by Fritzing 0.9.2b)
circuit board: 7.42245cm x 4.98122cm
breadboards: 1

parts:
  IC1 = attiny85 [package=dip]
  CR2032 = Battery Holders [package=battcom_20mm_pth]
  ISP = AVR ISP 6 Pin [package=2x3-ns]
  ON/OFF = SWITCH_SPDT [package=kps-1290]
  RADIO = RF-LINK_TX [package=rf-link_tx]
  R1 = Resistor [tolerance=±5% resistance=300 package=THT]
  LED1 = LED - 5mm [color="Blue (505nm)" package="5 mm [THT]"]
  R2 = Resistor [tolerance=±5% resistance=300 package=THT]
  LED2 = LED - 5mm [color="Green (565nm)" package="5 mm [THT]"]
  ANT = male pin header, 1 pin [form="♂ (male)"]
  TRIGGER = male pin header, 3 pins [form="♂ (male)"]
  MANUAL = Pushbutton [package="[THT]"]
  R3 = Resistor [tolerance=±5% resistance=1k package=THT]

nets (from the pcb view):
  N1: IC1.Pin_1, ISP.5
  N2: IC1.Pin_2, RADIO.+5V
  N3: IC1.Pin_3, RADIO.DATA, R1.Pin_0
  N4: IC1.Pin_4, CR2032.-, ISP.6, RADIO.GND, LED1.cathode, R2.Pin_1, TRIGGER.pin3
  N5: IC1.Pin_5, ISP.4, LED2.anode
  N6: IC1.Pin_6, ISP.1
  N7: IC1.Pin_7, ISP.3, R3.Pin_0
  N8: IC1.Pin_8, ISP.2, ON/OFF.O, TRIGGER.pin1, MANUAL.Pin_3, MANUAL.Pin_4
  N9: CR2032.+, ON/OFF.P
  N10: RADIO.ANT, ANT.pin1
  N11: R1.Pin_1, LED1.anode
  N12: R2.Pin_0, LED2.cathode
  N13: TRIGGER.pin2, MANUAL.Pin_1, MANUAL.Pin_2, R3.Pin_1
